# Fritzing sketch incubator (saved by Fritzing 0.9.6b)
circuit board: 22.1697cm x 18.2179cm
breadboards: 1

parts:
  Part1 = Arduino Uno (Rev3) - ICSP
  Q1 = NPN-Transistor [package="TO92 [THT]"]
  D1 = Rectifier Diode [part_number=1N4001 package="300 mil [THT]"]
  RE1 = Rotary Encoder [package=THT]
  C1 = Ceramic Capacitor [capacitance=0.1mF voltage=35V package="100 mil [THT, multilayer]"]
  K1 = Relay [part_number=FRS1B-S package=THT]
  U1 = LCD-16X2 [package=lcd-16x2]
  R1 = Resistor [tolerance=±5% power=0.25 resistance=220 package=THT]
  S1 = Pushbutton [package=THT]
  R2 = Resistor [tolerance=±5% power=0.25 resistance=22k package=THT]
  M1 = DC Motor
  R3 = Resistor [tolerance=±5% power=0.25 resistance=6.8 package=THT]
  V1 = DC Power [voltage=12V]
  Grove1 = Grove 3 Axis Digital Accelerometer 16g

nets:
  N1: Part1.ICSP_MISO, Part1.D12/MISO, K1.COIL2
  5V: Part1.5V, S1.leg1, Grove1.VCC
  N2: Part1.ICSP_SCK, Part1.D13/SCK, S1.leg0
  N3: Part1.ICSP_MOSI, R2.Pin_0
  N4: Part1.RESET, Grove1.SCL
  GND: Part1.GND, Q1.E, RE1.EncoderPinC, K1.COIL1, U1.VO, U1.R_W, U1.K, R3.Pin_0, V1.V-, Grove1.GND
  N5: Part1.RESET2, Grove1.SDA
  N6: Part1.D8, U1.E
  N7: Part1.D9_PWM, U1.RS
  N8: Part1.D2, RE1.EncoderPinA
  N9: Part1.D3_PWM, RE1.EncoderPinB
  N10: Part1.D4, U1.DB7
  N11: Part1.D5_PWM, U1.DB6
  N12: Part1.D6_PWM, U1.DB5
  N13: Part1.D7, U1.DB4
  N14: Part1.VIN, V1.V+
  N15: Q1.B, R2.Pin_1
  N16: Q1.C, D1.anode, M1.pin_2
  N17: D1.cathode, U1.VDD, M1.pin_1
  N18: C1.0, K1.A, R3.Pin_1
  N19: U1.A, R1.Pin_1
